// Logisim project ALU.circ as structural Verilog: 13 circuits, main circuit Ida ALU
// ALU
module Ida_ALU (
  input  [23:0] ALU_Source_1,
  input  [23:0] ALU_Source_2,
  input  [3:0] Operation,
  input  [23:0] ALU_Source_1_2,
  input  [23:0] ALU_Source_2_2,
  input  [3:0] ALU_Control,
  output [23:0] ALU_Result
);

  wire [23:0] add, \and , \or , rl, rr, signcomp, sll, sra, srl, sub, unsigncomp, \xor ;

  // Probe on ALU_Source_1
  // Probe on ALU_Source_2
  // Probe on Operation
  // Probe on ALU_Result
  // Probe on ALU_Source_1_2
  // Probe on ALU_Source_1_2
  sll u_sll (.in_1(ALU_Source_1_2), .in_2(ALU_Source_1_2), .out_3(sll));
  srl u_srl (.in_1(ALU_Source_1_2), .in_2(ALU_Source_1_2), .out_3(srl));
  sra u_sra (.in_1(ALU_Source_1_2), .in_2(ALU_Source_1_2), .out_3(sra));
  rotateleft rotateleft (.in_1(ALU_Source_1_2), .in_2(ALU_Source_1_2), .out_3(rl));
  rotateright rotateright (.in_1(ALU_Source_1_2), .in_2(ALU_Source_1_2), .out_3(rr));
  \and  u_and (.in_1(ALU_Source_1_2), .in_2(ALU_Source_1_2), .out_3(\and ));
  \or  u_or (.in_1(ALU_Source_1_2), .in_2(ALU_Source_1_2), .out_3(\or ));
  \xor  u_xor (.in_1(ALU_Source_1_2), .in_2(ALU_Source_1_2), .out_3(\xor ));
  add u_add (.in_1(ALU_Source_1_2), .in_2(ALU_Source_1_2), .out_3(add));
  sub u_sub (.in_1(ALU_Source_1_2), .in_2(ALU_Source_1_2), .out_3(sub));
  signcomp u_signcomp (.in_1(ALU_Source_1_2), .in_2(ALU_Source_1_2), .out_3(signcomp));
  unsigncomp u_unsigncomp (.in_1(ALU_Source_1_2), .in_2(ALU_Source_1_2), .out_3(unsigncomp));
  Multiplexer #(.select(4), .width(24)) multiplexer_1 (
    .in0(sll), .in1(srl), .in2(sra), .in3(rl), .in4(rr), .in5(\and ), .in6(\or ), .in7(\xor ), .in8(add),
    .in9(sub), .in10(add), .in11(add), .in12(signcomp), .in13(unsigncomp), .in14({24{1'b0}}),
    .in15({24{1'b0}}), .out(ALU_Result), .sel(Operation));  // open: en

  assign ALU_Source_2_2 = ALU_Source_1_2;

  // Other names for the same wires on the sheet: control[3:0] = ALU_Control; op[3:0] = Operation;
  //   result[23:0] = ALU_Result; s1[23:0] = ALU_Source_1; s2[23:0] = ALU_Source_2; source1[23:0] = ALU_Source_1_2;
  //   source2[23:0] = ALU_Source_1_2

  // Notes on the sheet:
  //   INPUTS
  //   INPUT PROBES
  //   DO NOT CROSS WIRES
  //   OVER THIS BOX
  //   DO NOT CROSS WIRES
  //   OVER THIS BOX
  //   DO NOT MOVE/ADD/CHANGE ANY INPUT OR OUTPUT PINS!
  //   OUTPUT PROBES
  //   OUTPUT
  //   SELECT THE REQUESTED RESULT
endmodule

module sll (
  input  [23:0] in_1,
  input  [23:0] in_2,
  output [23:0] out_3
);

  wire [4:0] bit_extender_1_out;

  Bit_Extender #(.in_width(24), .out_width(5)) bit_extender_1 (.in(in_2), .out(bit_extender_1_out));
  Shifter #(.width(24)) shifter_1 (.in(in_1), .\dist (bit_extender_1_out), .out(out_3));
endmodule

module srl (
  input  [23:0] in_1,
  input  [23:0] in_2,
  output [23:0] out_3
);

  wire [4:0] bit_extender_1_out;

  Bit_Extender #(.in_width(24), .out_width(5)) bit_extender_1 (.in(in_2), .out(bit_extender_1_out));
  Shifter #(.width(24), .shift("lr")) shifter_1 (.in(in_1), .\dist (bit_extender_1_out), .out(out_3));
endmodule

module sra (
  input  [23:0] in_1,
  input  [23:0] in_2,
  output [23:0] out_3
);

  wire [4:0] bit_extender_1_out;

  Bit_Extender #(.in_width(24), .out_width(5)) bit_extender_1 (.in(in_2), .out(bit_extender_1_out));
  Shifter #(.width(24), .shift("ar")) shifter_1 (.in(in_1), .\dist (bit_extender_1_out), .out(out_3));
endmodule

module rotateleft (
  input  [23:0] in_1,
  input  [23:0] in_2,
  output [23:0] out_3
);

  wire [4:0] bit_extender_1_out;

  Bit_Extender #(.in_width(24), .out_width(5)) bit_extender_1 (.in(in_2), .out(bit_extender_1_out));
  Shifter #(.width(24), .shift("rl")) shifter_1 (.in(in_1), .\dist (bit_extender_1_out), .out(out_3));
endmodule

module rotateright (
  input  [23:0] in_1,
  input  [23:0] in_2,
  output [23:0] out_3
);

  wire [4:0] bit_extender_1_out;

  Bit_Extender #(.in_width(24), .out_width(5)) bit_extender_1 (.in(in_2), .out(bit_extender_1_out));
  Shifter #(.width(24), .shift("rr")) shifter_1 (.in(in_1), .\dist (bit_extender_1_out), .out(out_3));
endmodule

module \and  (
  input  [23:0] in_1,
  input  [23:0] in_2,
  output [23:0] out_3
);

  assign out_3 = in_1 & in_2;  // AND_Gate and_1, 24 bits wide
endmodule

module \or  (
  input  [23:0] in_1,
  input  [23:0] in_2,
  output [23:0] out_3
);

  assign out_3 = in_1 | in_2;  // OR_Gate or_1, 24 bits wide
endmodule

module \xor  (
  input  [23:0] in_1,
  input  [23:0] in_2,
  output [23:0] out_3
);

  assign out_3 = in_1 ^ in_2;  // XOR_Gate xor_1, 24 bits wide
endmodule

module add (
  input  [23:0] in_1,
  input  [23:0] in_2,
  output [23:0] out_3
);

  Adder #(.width(24)) adder_1 (.a(in_1), .b(in_2), .out(out_3));  // open: cin, cout
endmodule

module sub (
  input  [23:0] in_1,
  input  [23:0] in_2,
  output [23:0] out_3
);

  Subtractor #(.width(24)) subtractor_1 (.a(in_1), .b(in_2), .out(out_3));  // open: bin, bout
endmodule

module signcomp (
  input  [23:0] in_1,
  input  [23:0] in_2,
  output [23:0] out_3
);

  wire comparator_1_eq, comparator_5_gt, comparator_6_eq, comparator_7_eq, comparator_8_lt;
  wire [5:0] not_1_out;

  Comparator #(.width(24)) comparator_1 (.a(in_1), .b(in_2), .eq(comparator_1_eq));  // open: gt, lt
  Comparator #(.width(24)) comparator_2 (.a(in_1), .b(in_2), .gt(not_1_out[1]));  // open: eq, lt
  Comparator #(.width(24)) comparator_3 (.a(in_1), .b(in_2), .eq(not_1_out[2]));  // open: gt, lt
  Comparator #(.width(24)) comparator_4 (.a(in_1), .b(in_2), .lt(not_1_out[3]));  // open: gt, eq
  Comparator #(.width(24)) comparator_5 (.a(in_1), .b(in_2), .gt(comparator_5_gt));  // open: eq, lt
  Comparator #(.width(24)) comparator_6 (.a(in_1), .b(in_2), .eq(comparator_6_eq));  // open: gt, lt
  Comparator #(.width(24)) comparator_7 (.a(in_1), .b(in_2), .eq(comparator_7_eq));  // open: gt, lt
  Comparator #(.width(24)) comparator_8 (.a(in_1), .b(in_2), .lt(comparator_8_lt));  // open: gt, eq
  not not_1 (not_1_out[0], comparator_1_eq);
  or or_1 (not_1_out[5], comparator_7_eq, comparator_8_lt);
  or or_2 (not_1_out[4], comparator_5_gt, comparator_6_eq);
  assign out_3 = {{16{1'b0}}, {2'b01, not_1_out}};  // Bit_Extender bit_extender_1

  // Other names for the same wires on the sheet: input1[23:0] = in_1; input2[23:0] = in_2; output[23:0] = out_3
endmodule

module unsigncomp (
  input  [23:0] in_1,
  input  [23:0] in_2,
  output [23:0] out_3
);

  wire comparator_1_eq, comparator_5_gt, comparator_6_eq, comparator_7_eq, comparator_8_lt;
  wire [5:0] not_1_out;

  Comparator #(.width(24), .mode("unsigned")) comparator_1 (.a(in_1), .b(in_2), .eq(comparator_1_eq));  // open: gt, lt
  Comparator #(.width(24), .mode("unsigned")) comparator_2 (.a(in_1), .b(in_2), .gt(not_1_out[1]));  // open: eq, lt
  Comparator #(.width(24), .mode("unsigned")) comparator_3 (.a(in_1), .b(in_2), .eq(not_1_out[2]));  // open: gt, lt
  Comparator #(.width(24), .mode("unsigned")) comparator_4 (.a(in_1), .b(in_2), .lt(not_1_out[3]));  // open: gt, eq
  Comparator #(.width(24), .mode("unsigned")) comparator_5 (.a(in_1), .b(in_2), .gt(comparator_5_gt));  // open: eq, lt
  Comparator #(.width(24), .mode("unsigned")) comparator_6 (.a(in_1), .b(in_2), .eq(comparator_6_eq));  // open: gt, lt
  Comparator #(.width(24), .mode("unsigned")) comparator_7 (.a(in_1), .b(in_2), .eq(comparator_7_eq));  // open: gt, lt
  Comparator #(.width(24), .mode("unsigned")) comparator_8 (.a(in_1), .b(in_2), .lt(comparator_8_lt));  // open: gt, eq
  not not_1 (not_1_out[0], comparator_1_eq);
  or or_1 (not_1_out[5], comparator_7_eq, comparator_8_lt);
  or or_2 (not_1_out[4], comparator_5_gt, comparator_6_eq);
  assign out_3 = {{16{1'b0}}, {2'b01, not_1_out}};  // Bit_Extender bit_extender_1

  // Other names for the same wires on the sheet: input1[23:0] = in_1; input2[23:0] = in_2; output[23:0] = out_3
endmodule
