// Logisim project CPU.circ as structural Verilog: 1 circuit, main circuit Ida CPU
// CPU
module Ida_CPU (
  input  [31:0] Instruction,
  input  Clock,
  output [23:0] Mem_Data,
  output [23:0] Mem_Address,
  output Mem_Write,
  output [23:0] Next_PC,
  output [23:0] r00,
  output [23:0] r01,
  output [23:0] r02,
  output [23:0] r03,
  output [23:0] r04,
  output [23:0] r05,
  output [23:0] r06,
  output [23:0] r07,
  output [23:0] r08,
  output [23:0] r09,
  output [23:0] r10,
  output [23:0] r11,
  output [23:0] r12,
  output [23:0] r13,
  output [23:0] r14,
  output [23:0] r15
);

  wire a1, a2, a3, comparator_2_gt, comparator_3_lt, comparator_8_lt, comparator_10_eq, jump, link, load,
       multiplexer_11_out, nand_1_out, not_1_out, regWrite;
  wire [1:0] multiplexer_1_out, \type ;
  wire [3:0] multiplexer_12_out;
  wire [23:0] adder_2_out, ALU_output, bit_extender_1_out, bit_extender_2_out, bit_extender_5_out, cr,
       ida_register_file_1_reg_1_value, ida_register_file_1_reg_2_value, multiplexer_3_out,
       multiplexer_6_out, multiplexer_7_out, multiplexer_9_out, multiplexer_10_out, RAM_output, rd,
       register_2_q, ri, rs;

  // Probe on Instruction
  // Probe on Clock
  // Probe on r00
  // Probe on r01
  // Probe on r02
  // Probe on r03
  // Probe on r04
  // Probe on r05
  // Probe on r06
  // Probe on r07
  // Probe on Mem_Data
  // Probe on Mem_Address
  // Probe on Mem_Write
  // Probe on Next_PC
  Multiplexer #(.width(2), .enable("false")) multiplexer_1 (
    .in0(2'b11), .in1(2'b01), .out(multiplexer_1_out), .sel(a1));
  assign bit_extender_1_out = {{4{Instruction[19]}}, Instruction[19:0]};  // Bit_Extender bit_extender_1
  assign bit_extender_2_out = {{8{Instruction[15]}}, Instruction[15:0]};  // Bit_Extender bit_extender_2
  assign rd = {{20{1'b0}}, Instruction[23:20]};  // Bit_Extender bit_extender_3
  assign rs = {{20{1'b0}}, Instruction[19:16]};  // Bit_Extender bit_extender_4
  // Probe on r08
  // Probe on r09
  // Probe on r10
  // Probe on r11
  // Probe on r12
  // Probe on r13
  // Probe on r14
  // Probe on r15
  Multiplexer #(.width(2), .enable("false")) multiplexer_2 (
    .in0(multiplexer_1_out), .in1(2'b10), .out(\type ), .sel(a2));
  assign bit_extender_5_out = {{20{1'b0}}, Instruction[3:0]};  // Bit_Extender bit_extender_5
  Multiplexer #(.select(2), .width(24), .enable("false")) multiplexer_3 (
    .in1(Instruction[23:0]), .in2(bit_extender_1_out), .in3(bit_extender_2_out), .out(multiplexer_3_out),
    .sel(\type ));  // open: in0
  // Probe on a2
  Multiplexer #(.width(24), .enable("false")) multiplexer_4 (
    .in0(bit_extender_5_out), .in1(multiplexer_3_out), .out(ri), .sel(Instruction[24]));
  // Probe on a3
  Comparator #(.width(4)) comparator_1 (.a(Instruction[31:28]), .b(4'b1100), .lt(a3));  // open: gt, eq
  Comparator #(.width(4)) comparator_2 (.a(Instruction[31:28]), .b(4'b1011), .gt(comparator_2_gt));  // open: eq, lt
  Comparator #(.width(4)) comparator_3 (.a(Instruction[31:28]), .b(4'b1110), .lt(comparator_3_lt));  // open: gt, eq
  // Probe on a1
  Comparator #(.width(4)) comparator_4 (.a(Instruction[31:28]), .b(4'b1101), .gt(a1));  // open: eq, lt
  Comparator #(.width(4)) comparator_5 (.a(Instruction[31:28]), .b(4'b1010), .eq(load));  // open: gt, lt
  Comparator #(.width(4)) comparator_6 (.a(Instruction[31:28]), .b(4'b1011), .eq(Mem_Write));  // open: gt, lt
  Comparator #(.width(4)) comparator_7 (.a(Instruction[31:28]), .b(4'b1111), .eq(jump));  // open: gt, lt
  Comparator #(.width(4)) comparator_8 (.a(Instruction[31:28]), .b(4'b1100), .lt(comparator_8_lt));  // open: gt, eq
  Comparator #(.width(4)) comparator_9 (.a(Instruction[31:28]), .b(4'b1110), .eq(link));  // open: gt, lt
  Multiplexer #(.width(24), .enable("false")) multiplexer_5 (.in1(r02), .out(rd), .sel(link));  // open: in0
  // Probe on a2
  and and_1 (a2, comparator_2_gt, comparator_3_lt);
  or or_1 (regWrite, comparator_8_lt, link);
  Register #(.width(24)) register_1 (.D(multiplexer_6_out), .Q(cr), .clk(Clock));  // open: en, clr
  Multiplexer #(.width(24), .enable("false")) multiplexer_6 (
    .in1(ALU_output), .out(multiplexer_6_out), .sel(a2));  // open: in0
  Register #(.width(24)) register_2 (.D(Next_PC), .Q(register_2_q), .clk(Clock));  // open: en, clr
  Multiplexer #(.width(24), .enable("false")) multiplexer_7 (
    .in0(ALU_output), .in1(ri), .out(multiplexer_7_out), .sel(link));
  Adder #(.width(24)) adder_1 (.a(rs), .b(ri), .out(Mem_Address));  // open: cin, cout
  Adder #(.width(24)) adder_2 (.a(register_2_q), .b(24'h1), .out(adder_2_out));  // open: cin, cout
  Multiplexer #(.width(24), .enable("false")) multiplexer_8 (
    .in0(adder_2_out), .in1(Instruction[23:0]), .out(Next_PC), .sel(jump));
  Ida_Register_File ida_register_file_1 (
    .Read_Reg_1(rs[3:0]), .Read_Reg_2(ri[3:0]), .Write_Reg(rd[3:0]), .Write_Value(multiplexer_9_out),
    .Reg_1_Value(ida_register_file_1_reg_1_value), .Reg_2_Value(ida_register_file_1_reg_2_value),
    .Reg_Write(regWrite), .Clock(Clock), .r00(r00), .r01(r01), .r02(r02), .r03(r03), .r04(r04), .r05(r05),
    .r06(r06), .r07(r07), .r08(r08), .r09(r09), .r10(r10), .r11(r11), .r12(r12), .r13(r13), .r14(r14),
    .r15(r15), .Reg_3_Value(Mem_Data));
  Multiplexer #(.width(24), .enable("false")) multiplexer_9 (
    .in0(multiplexer_7_out), .in1(RAM_output), .out(multiplexer_9_out), .sel(load));
  Multiplexer #(.width(24), .enable("false")) multiplexer_10 (
    .in0(ida_register_file_1_reg_2_value), .in1(ri), .out(multiplexer_10_out), .sel(Instruction[24]));
  Multiplexer #(.select(3), .enable("false")) multiplexer_11 (
    .in0(cr[0]), .in1(cr[1]), .in2(cr[2]), .in3(cr[3]), .in4(cr[4]), .in5(cr[5]), .in6(cr[6]), .in7(cr[7]),
    .out(multiplexer_11_out), .sel(Instruction[27:25]));
  Comparator #(.width(3)) comparator_10 (.a(Instruction[27:25]), .b(3'b000), .eq(comparator_10_eq));  // open: gt, lt
  not not_1 (not_1_out, comparator_10_eq);
  RAM #(.addrWidth(24), .dataWidth(24), .bus("separate")) ram_1 (
    .addr(Mem_Address), .din(Mem_Data), .data(RAM_output), .str(Mem_Write), .clk(Clock), .ld(load));  // open: sel, clr
  Ida_ALU ida_alu_1 (
    .ALU_Source_2(multiplexer_10_out), .Operation(multiplexer_12_out), .ALU_Result(ALU_output),
    .ALU_Source_1_2(ida_register_file_1_reg_1_value));  // open: ALU_Source_1, ALU_Source_2_2, ALU_Control
  Multiplexer #(.width(4), .enable("false")) multiplexer_12 (
    .in0(Instruction[31:28]), .in1(4'b1111), .out(multiplexer_12_out), .sel(nand_1_out));
  nand nand_1 (nand_1_out, multiplexer_11_out, not_1_out);

  // Other names for the same wires on the sheet: clk = Clock; bb[23:0] = Instruction[23:0]; inst[31:0] = Instruction;
  //   ALUsrc = Instruction[24]; imm = Instruction[24]; cq[2:0] = Instruction[27:25]; op[3:0] = Instruction[31:28];
  //   memAddr[23:0] = Mem_Address; memData[23:0] = Mem_Data; memWrite = Mem_Write; nextPC[23:0] = Next_PC

  // Notes on the sheet:
  //   INPUTS
  //   INPUT PROBES
  //   OUTPUT PROBES
  //   OUTPUTS
  //   DO NOT MOVE/ADD/CHANGE ANY INPUT OR OUTPUT PINS!
endmodule
