// Logisim project REG.circ as structural Verilog: 1 circuit, main circuit Ida Register File
// Register File
module Ida_Register_File (
  input  [3:0] Read_Reg_1,
  input  [3:0] Read_Reg_2,
  input  [3:0] Write_Reg,
  input  [23:0] Write_Value,
  input  Reg_Write,
  input  Clock,
  output [23:0] Reg_1_Value,
  output [23:0] Reg_2_Value,
  output [23:0] Reg_3_Value,
  output [23:0] r00,
  output [23:0] r01,
  output [23:0] r02,
  output [23:0] r03,
  output [23:0] r04,
  output [23:0] r05,
  output [23:0] r06,
  output [23:0] r07,
  output [23:0] r08,
  output [23:0] r09,
  output [23:0] r10,
  output [23:0] r11,
  output [23:0] r12,
  output [23:0] r13,
  output [23:0] r14,
  output [23:0] r15
);

  wire demultiplexer_1_out0, demultiplexer_1_out1, demultiplexer_1_out2, demultiplexer_1_out3,
       demultiplexer_1_out4, demultiplexer_1_out5, demultiplexer_1_out6, demultiplexer_1_out7,
       demultiplexer_1_out8, demultiplexer_1_out9, demultiplexer_1_out10, demultiplexer_1_out11,
       demultiplexer_1_out12, demultiplexer_1_out13, demultiplexer_1_out14, demultiplexer_1_out15;

  // Probe on Read_Reg_1
  // Probe on Read_Reg_2
  // Probe on Write_Reg
  // Probe on Write_Value
  // Probe on Reg_Write
  // Probe on Clock
  // Probe on Reg_1_Value
  // Probe on Reg_2_Value
  // Probe on Reg_3_Value
  // Probe on r00
  // Probe on r01
  // Probe on r02
  // Probe on r03
  // Probe on r04
  // Probe on r05
  // Probe on r06
  // Probe on r07
  // Probe on r08
  // Probe on r09
  // Probe on r10
  // Probe on r11
  // Probe on r12
  // Probe on r13
  // Probe on r14
  // Probe on r15
  Multiplexer #(.select(4), .width(24)) multiplexer_1 (
    .in0(r00), .in1(r01), .in2(r02), .in3(r03), .in4(r04), .in5(r05), .in6(r06), .in7(r07), .in8(r08),
    .in9(r09), .in10(r10), .in11(r11), .in12(r12), .in13(r13), .in14(r14), .in15(r15), .out(Reg_3_Value),
    .sel(Write_Reg));  // open: en
  Demultiplexer #(.select(4)) demultiplexer_1 (
    .out0(demultiplexer_1_out0), .out1(demultiplexer_1_out1), .out2(demultiplexer_1_out2),
    .out3(demultiplexer_1_out3), .out4(demultiplexer_1_out4), .out5(demultiplexer_1_out5),
    .out6(demultiplexer_1_out6), .out7(demultiplexer_1_out7), .out8(demultiplexer_1_out8),
    .out9(demultiplexer_1_out9), .out10(demultiplexer_1_out10), .out11(demultiplexer_1_out11),
    .out12(demultiplexer_1_out12), .out13(demultiplexer_1_out13), .out14(demultiplexer_1_out14),
    .out15(demultiplexer_1_out15), .in(Reg_Write), .sel(Write_Reg));  // open: en
  Multiplexer #(.select(4), .width(24)) multiplexer_2 (
    .in0(r00), .in1(r01), .in2(r02), .in3(r03), .in4(r04), .in5(r05), .in6(r06), .in7(r07), .in8(r08),
    .in9(r09), .in10(r10), .in11(r11), .in12(r12), .in13(r13), .in14(r14), .in15(r15), .out(Reg_2_Value),
    .sel(Read_Reg_2));  // open: en
  Register #(.width(24)) register_1 (.D(Write_Value), .en(demultiplexer_1_out0), .Q(r00), .clk(Clock));  // open: clr
  Register #(.width(24)) register_2 (.D(Write_Value), .en(demultiplexer_1_out1), .Q(r01), .clk(Clock));  // open: clr
  Register #(.width(24)) register_3 (.D(Write_Value), .en(demultiplexer_1_out2), .Q(r02), .clk(Clock));  // open: clr
  Register #(.width(24)) register_4 (.D(Write_Value), .en(demultiplexer_1_out3), .Q(r03), .clk(Clock));  // open: clr
  Register #(.width(24)) register_5 (.D(Write_Value), .en(demultiplexer_1_out4), .Q(r04), .clk(Clock));  // open: clr
  Register #(.width(24)) register_6 (.D(Write_Value), .en(demultiplexer_1_out5), .Q(r05), .clk(Clock));  // open: clr
  Register #(.width(24)) register_7 (.D(Write_Value), .en(demultiplexer_1_out6), .Q(r06), .clk(Clock));  // open: clr
  Register #(.width(24)) register_8 (.D(Write_Value), .en(demultiplexer_1_out7), .Q(r07), .clk(Clock));  // open: clr
  Register #(.width(24)) register_9 (.D(Write_Value), .en(demultiplexer_1_out8), .Q(r08), .clk(Clock));  // open: clr
  Register #(.width(24)) register_10 (.D(Write_Value), .en(demultiplexer_1_out9), .Q(r09), .clk(Clock));  // open: clr
  Register #(.width(24)) register_11 (.D(Write_Value), .en(demultiplexer_1_out10), .Q(r10), .clk(Clock));  // open: clr
  Register #(.width(24)) register_12 (.D(Write_Value), .en(demultiplexer_1_out11), .Q(r11), .clk(Clock));  // open: clr
  Register #(.width(24)) register_13 (.D(Write_Value), .en(demultiplexer_1_out12), .Q(r12), .clk(Clock));  // open: clr
  Register #(.width(24)) register_14 (.D(Write_Value), .en(demultiplexer_1_out13), .Q(r13), .clk(Clock));  // open: clr
  Register #(.width(24)) register_15 (.D(Write_Value), .en(demultiplexer_1_out14), .Q(r14), .clk(Clock));  // open: clr
  Register #(.width(24)) register_16 (.D(Write_Value), .en(demultiplexer_1_out15), .Q(r15), .clk(Clock));  // open: clr
  Multiplexer #(.select(4), .width(24)) multiplexer_3 (
    .in0(r00), .in1(r01), .in2(r02), .in3(r03), .in4(r04), .in5(r05), .in6(r06), .in7(r07), .in8(r08),
    .in9(r09), .in10(r10), .in11(r11), .in12(r12), .in13(r13), .in14(r14), .in15(r15), .out(Reg_1_Value),
    .sel(Read_Reg_1));  // open: en

  // Other names for the same wires on the sheet: clk = Clock; reg1Read[3:0] = Read_Reg_1; reg1Val[23:0] = Reg_1_Value;
  //   reg2Read[3:0] = Read_Reg_2; reg2Val[23:0] = Reg_2_Value; reg3Val[23:0] = Reg_3_Value;
  //   reg3Write[3:0] = Write_Reg; write = Reg_Write; writeVal[23:0] = Write_Value

  // Notes on the sheet:
  //   INPUT PINS
  //   INPUT PROBES
  //   OUTPUT PROBES
  //   OUTPUT PINS
  //   DO NOT MOVE/ADD/CHANGE ANY INPUT OR OUTPUT PINS!
endmodule
